// Logisim project ex5.circ as structural Verilog: 5 circuits, main circuit rotr
module rotr (
  input  [15:0] A,
  input  [3:0] B,
  output [15:0] Out1
);

  wire [15:0] rot1_1_out_3, rot2_1_out_3, rot4_1_out_3;

  rot1 rot1_1 (.in_1(A), .Enable(B[0]), .out_3(rot1_1_out_3));
  rot2 rot2_1 (.in_1(rot1_1_out_3), .Enable(B[1]), .out_3(rot2_1_out_3));
  rot4 rot4_1 (.in_1(rot2_1_out_3), .Enable(B[2]), .out_3(rot4_1_out_3));
  rot8 rot8_1 (.in_1(rot4_1_out_3), .Enable(B[3]), .out_3(Out1));

  // Notes on the sheet:
  //   PUT CIRCUITRY HERE
endmodule

module rot8 (
  input  [15:0] in_1,
  input  Enable,
  output [15:0] out_3
);

  wire not_1_out;
  wire [15:0] multiplexer_1_out, multiplexer_2_out;

  Multiplexer #(.enable("false"), .width(16)) multiplexer_1 (
    .in0({16{1'b0}}), .in1(in_1), .out(multiplexer_1_out), .sel(Enable));
  not not_1 (not_1_out, Enable);
  Multiplexer #(.enable("false"), .width(16)) multiplexer_2 (
    .in0({16{1'b0}}), .in1(in_1), .out(multiplexer_2_out), .sel(not_1_out));
  assign out_3 = {multiplexer_1_out[7:0], multiplexer_1_out[15:8]} | multiplexer_2_out;  // OR_Gate or_1, 16 bits wide

  // Notes on the sheet:
  //   PUT CIRCUITRY HERE
endmodule

module rot4 (
  input  [15:0] in_1,
  input  Enable,
  output [15:0] out_3
);

  wire not_1_out;
  wire [15:0] multiplexer_1_out, multiplexer_2_out;

  Multiplexer #(.enable("false"), .width(16)) multiplexer_1 (
    .in0({16{1'b0}}), .in1(in_1), .out(multiplexer_1_out), .sel(Enable));
  not not_1 (not_1_out, Enable);
  Multiplexer #(.enable("false"), .width(16)) multiplexer_2 (
    .in0({16{1'b0}}), .in1(in_1), .out(multiplexer_2_out), .sel(not_1_out));
  assign out_3 = {multiplexer_1_out[3:0], multiplexer_1_out[15:4]} | multiplexer_2_out;  // OR_Gate or_1, 16 bits wide

  // Notes on the sheet:
  //   PUT CIRCUITRY HERE
endmodule

module rot2 (
  input  [15:0] in_1,
  input  Enable,
  output [15:0] out_3
);

  wire not_1_out;
  wire [15:0] multiplexer_1_out, multiplexer_2_out;

  Multiplexer #(.enable("false"), .width(16)) multiplexer_1 (
    .in0({16{1'b0}}), .in1(in_1), .out(multiplexer_1_out), .sel(Enable));
  not not_1 (not_1_out, Enable);
  Multiplexer #(.enable("false"), .width(16)) multiplexer_2 (
    .in0({16{1'b0}}), .in1(in_1), .out(multiplexer_2_out), .sel(not_1_out));
  assign out_3 = {multiplexer_1_out[1:0], multiplexer_1_out[15:2]} | multiplexer_2_out;  // OR_Gate or_1, 16 bits wide

  // Notes on the sheet:
  //   PUT CIRCUITRY HERE
endmodule

module rot1 (
  input  [15:0] in_1,
  input  Enable,
  output [15:0] out_3
);

  wire not_1_out;
  wire [15:0] multiplexer_1_out, multiplexer_2_out;

  Multiplexer #(.enable("false"), .width(16)) multiplexer_1 (
    .in0({16{1'b0}}), .in1(in_1), .out(multiplexer_1_out), .sel(Enable));
  not not_1 (not_1_out, Enable);
  Multiplexer #(.enable("false"), .width(16)) multiplexer_2 (
    .in0({16{1'b0}}), .in1(in_1), .out(multiplexer_2_out), .sel(not_1_out));
  assign out_3 = {multiplexer_1_out[0], multiplexer_1_out[15:1]} | multiplexer_2_out;  // OR_Gate or_1, 16 bits wide

  // Notes on the sheet:
  //   PUT CIRCUITRY HERE
endmodule
