// Logisim project branch_comp.circ as structural Verilog: 1 circuit, main circuit branch_comp
module branch_comp (
  input  [31:0] rs1,
  input  [31:0] rs2,
  input  BrUn,
  output BrEq,
  output BrLt
);

  wire comparator_1_eq, not_1_out, Signed_Res, Unsigned_Res;
  wire [31:0] subtractor_1_out;

  Comparator #(.width(32)) comparator_1 (.a(rs1), .b(rs2), .eq(comparator_1_eq));  // open: gt, lt
  Subtractor #(.width(32)) subtractor_1 (.a(rs1), .b(rs2), .out(subtractor_1_out));  // open: bin, bout
  Comparator #(.width(32)) comparator_2 (.a(rs1), .b(rs2), .eq(Signed_Res));  // open: gt, lt
  not not_1 (not_1_out, subtractor_1_out[31]);
  and and_1 (Unsigned_Res, comparator_1_eq, not_1_out);
  Multiplexer #(.enable("false")) multiplexer_1 (.in0(Signed_Res), .in1(Unsigned_Res), .out(BrEq), .sel(BrUn));
  not not_2 (BrLt, BrEq);

  // Other names for the same wires on the sheet: Type_Res = BrEq

  // Notes on the sheet:
  //   INPUTS to your circuit
  //   DON'T CHANGE THE LOCATIONS OF THE INPUTS AND OUTPUTS!
  //   OUTPUT from your circuit
endmodule
