// Logisim project control_logic.circ as structural Verilog: 1 circuit, main circuit control_logic
module control_logic (
  input  [31:0] inst,
  input  BrEq,
  input  BrLt,
  output PCSel,
  output RegWEn,
  output [2:0] ImmSel,
  output BrUn,
  output ASel,
  output BSel,
  output [3:0] ALUSel,
  output MemRW,
  output [1:0] WBSel,
  output CSRSel,
  output CSRWen
);

  wire not_1_out, not_2_out, not_3_out;
  wire [2:0] BranchType;

  not not_1 (not_1_out, BrEq);
  not not_2 (not_2_out, BrLt);
  not not_3 (not_3_out, BrLt);
  Multiplexer #(.enable("false"), .select(3)) multiplexer_1 (
    .in0(1'b0), .in1(1'b1), .in2(BrEq), .in3(not_1_out), .in4(BrLt), .in5(not_2_out), .in6(BrLt),
    .in7(not_3_out), .out(PCSel), .sel(BranchType));
  ROM #(.addrWidth(17), .dataWidth(19)) rom_1 (
    .addr({inst[31:25], inst[14:12], inst[6:0]}),
    .data({CSRWen, CSRSel, WBSel, MemRW, ALUSel, BSel, ASel, BrUn, ImmSel, RegWEn, BranchType}));

  // Other names for the same wires on the sheet: rd[4:0] = inst[11:7]; rs1[4:0] = inst[19:15]; rs2[4:0] = inst[24:20];
  //   opcode[6:0] = inst[6:0]; ROMAddress[16:0] = {inst[31:25], inst[14:12], inst[6:0]}; funct3[2:0] = inst[14:12];
  //   funct7[6:0] = inst[31:25]

  // Notes on the sheet:
  //   INPUTS to your circuit
  //   contents of rom_1 (hex, n*v repeats v):
  //   0 0 0 8218 15*0 218 0 0 0 348 11*0 4220 15*0 8 0 0 0 248 43*0 432 0 0 0 10219 7*0 10359 0 0 0 10
  //   15*0 8218 15*0 1618 15*0 4220 15*0 1408 47*0 433 15*0 7a868 15*0 8218 15*0 2218 15*0 4220 15*0 2008
  //   63*0 3a868 31*0 2698 31*0 2488 63*0 3a868 15*0 8218 15*0 1218 31*0 1008 47*0 2034 31*0 8218 15*0
  //   1a18 31*0 1808 47*0 2035 15*0 7a868 31*0 e18 31*0 c08 47*0 24b6 15*0 3a868 31*0 a18 31*0 808 47*0
  //   24b7 15*0 3a868 63*0 2c08 63*0 10 63*0 3008 127*0 3488 127*0 3888 31359*0 408 607*0 1e18 31*0 1c08
  //   DON'T CHANGE THE LOCATIONS OF THE INPUTS AND OUTPUTS!
  //   OUTPUT from your circuit
endmodule
