// Logisim project cpu.circ as structural Verilog: 6 circuits, main circuit cpu
module cpu (
  input  clk,
  input  [31:0] INSTRUCTION,
  input  [31:0] READ_DATA,
  output [31:0] WRITE_ADDRESS,
  output [31:0] PROGRAM_COUNTER,
  output [31:0] ra,
  output [31:0] sp,
  output [31:0] t0,
  output [31:0] t1,
  output [31:0] t2,
  output [31:0] s0,
  output [31:0] s1,
  output [31:0] a0,
  output [31:0] tohost,
  output [3:0] WRITE_ENABLE,
  output [31:0] WRITE_DATA
);

  wire ASel, BJK, BrEq, BrLt, BrUn, BSel, CSRSel, CSRWen, EX_ASel, EX_BrEq, EX_BrLt, EX_BrUn, EX_BSel,
       EX_CSRSel, EX_CSRWen, EX_MemRW, EX_RegWEn, Freeze_Pipeline, Halt_Signal, MA_CSRSel, MA_CSRWen,
       MA_MemRW, MA_RegWEn, MemRW, multiplexer_2_out, multiplexer_3_out, multiplexer_4_out,
       multiplexer_5_out, multiplexer_6_out, multiplexer_8_out, multiplexer_9_out, multiplexer_10_out,
       multiplexer_12_out, or_1_out, PCSel, RegWEn, Stall_Signal, WB_CSRSel, WB_CSRWen, WB_RegWEn;
  wire [1:0] EX_WBSel, ForwardA, ForwardB, MA_WBSel, multiplexer_7_out, WB_WBSel, WBSel;
  wire [2:0] EX_funct3, funct3, ImmSel;
  wire [3:0] ALUSel, EX_ALUSel, multiplexer_11_out;
  wire [4:0] EX_rd, MA_rd, WB_rd;
  wire [6:0] EX_funct7, funct7;
  wire [24:0] EX_Inst, ID_Inst;
  wire [31:0] adder_1_out, ALU_Res, CSR_Value, EX_MA_RD2, EX_PC, EX_RD1, EX_RD2, ID_Inst_Input, ID_PC, imm,
       MA_Inst, MA_PC, multiplexer_1_out, multiplexer_13_out, multiplexer_14_out, multiplexer_18_out,
       multiplexer_19_out, Read_Data_1, Read_Data_2, WB_Inst, WB_WD, Write_Data_t;

  Adder #(.width(32)) adder_1 (.a(PROGRAM_COUNTER), .b(32'h4), .out(adder_1_out));  // open: cin, cout
  or or_1 (or_1_out, PCSel, BJK);
  Multiplexer #(.enable("false"), .width(32)) multiplexer_1 (
    .in0(adder_1_out), .in1(WRITE_ADDRESS), .out(multiplexer_1_out), .sel(or_1_out));
  Register #(.width(32)) PC (.D(multiplexer_1_out), .clk(clk), .Q(PROGRAM_COUNTER));  // open: en, clr
  Register #(.width(32)) IF_ID_PC_Reg (.D(PROGRAM_COUNTER), .clk(clk), .Q(ID_PC));  // open: en, clr
  Register #(.width(32)) IF_ID_Instr_Reg (
    .D(INSTRUCTION), .clk(clk), .Q({funct7, ID_Inst[24:15], funct3, ID_Inst[11:0]}));  // open: en, clr
  Multiplexer #(.enable("false")) multiplexer_2 (.in0(RegWEn), .in1(1'b0), .out(multiplexer_2_out), .sel(Stall_Signal));
  Multiplexer #(.enable("false")) multiplexer_3 (.in0(BrEq), .in1(1'b0), .out(multiplexer_3_out), .sel(Stall_Signal));
  Multiplexer #(.enable("false")) multiplexer_4 (.in0(BrLt), .in1(1'b0), .out(multiplexer_4_out), .sel(Stall_Signal));
  Multiplexer #(.enable("false")) multiplexer_5 (.in0(BrUn), .in1(1'b0), .out(multiplexer_5_out), .sel(Stall_Signal));
  Multiplexer #(.enable("false")) multiplexer_6 (.in0(MemRW), .in1(1'b0), .out(multiplexer_6_out), .sel(Stall_Signal));
  Multiplexer #(.enable("false"), .width(2)) multiplexer_7 (
    .in0(WBSel), .in1(2'b00), .out(multiplexer_7_out), .sel(Stall_Signal));
  Multiplexer #(.enable("false")) multiplexer_8 (.in0(CSRSel), .in1(1'b0), .out(multiplexer_8_out), .sel(Stall_Signal));
  Multiplexer #(.enable("false")) multiplexer_9 (.in0(CSRWen), .in1(1'b0), .out(multiplexer_9_out), .sel(Stall_Signal));
  Register #(.width(32)) ID_EX_PC_Reg (.D(ID_PC), .clk(clk), .Q(EX_PC));  // open: en, clr
  Register #(.width(32)) ID_EX_Inst_Reg (
    .D(ID_Inst_Input), .clk(clk), .Q({EX_funct7, EX_Inst[24:15], EX_funct3, EX_Inst[11:0]}));  // open: en, clr
  Register #(.width(32)) ID_EX_RD1_Reg (.D(Read_Data_1), .clk(clk), .Q(EX_RD1));  // open: en, clr
  Register #(.width(5)) ID_EX_RD_Reg (.D(ID_Inst[11:7]), .clk(clk), .Q(EX_rd));  // open: en, clr
  Register #(.width(1)) ID_EX_RegWEn_Reg (.D(multiplexer_2_out), .clk(clk), .Q(EX_RegWEn));  // open: en, clr
  Register #(.width(1)) ID_EX_BrEq_Reg (.D(multiplexer_3_out), .clk(clk), .Q(EX_BrEq));  // open: en, clr
  Register #(.width(1)) ID_EX_BrLt_Reg (.D(multiplexer_4_out), .clk(clk), .Q(EX_BrLt));  // open: en, clr
  Register #(.width(1)) ID_EX_BrUn_Reg (.D(multiplexer_5_out), .clk(clk), .Q(EX_BrUn));  // open: en, clr
  Register #(.width(1)) ID_EX_MemRW_Reg (.D(multiplexer_6_out), .clk(clk), .Q(EX_MemRW));  // open: en, clr
  Register #(.width(2)) ID_EX_WBSel_reg (.D(multiplexer_7_out), .clk(clk), .Q(EX_WBSel));  // open: en, clr
  Register #(.width(1)) ID_EX_CSRSel_Reg (.D(multiplexer_8_out), .clk(clk), .Q(EX_CSRSel));  // open: en, clr
  Register #(.width(1)) ID_EX_CSRWen_Reg (.D(multiplexer_9_out), .clk(clk), .Q(EX_CSRWen));  // open: en, clr
  Register #(.width(32)) EX_MA_PC_Reg (.D(EX_PC), .clk(clk), .Q(MA_PC));  // open: en, clr
  Register #(.width(32)) EX_MA_Inst_Reg (
    .D({EX_funct7, EX_Inst[24:15], EX_funct3, EX_Inst[11:0]}), .clk(clk), .Q(MA_Inst));  // open: en, clr
  Register #(.width(32)) ID_EX_RD2_Reg (.D(Read_Data_2), .clk(clk), .Q(EX_RD2));  // open: en, clr
  Register #(.width(5)) EX_AM_RD_Reg (.D(EX_rd), .clk(clk), .Q(MA_rd));  // open: en, clr
  Register #(.width(1)) EX_MA_RegWEn_Reg (.D(EX_RegWEn), .clk(clk), .Q(MA_RegWEn));  // open: en, clr
  Register #(.width(32)) EX_MA_ALU_Reg (.D(ALU_Res), .clk(clk), .Q(WRITE_ADDRESS));  // open: en, clr
  Register #(.width(1)) ID_EX_ASel_Reg (.D(multiplexer_10_out), .clk(clk), .Q(EX_ASel));  // open: en, clr
  Multiplexer #(.enable("false")) multiplexer_10 (.in0(ASel), .in1(1'b0), .out(multiplexer_10_out), .sel(Stall_Signal));
  Register #(.width(4)) ID_EX_ALUSel_Reg (.D(multiplexer_11_out), .clk(clk), .Q(EX_ALUSel));  // open: en, clr
  Multiplexer #(.enable("false"), .width(4)) multiplexer_11 (
    .in0(ALUSel), .in1(4'b0000), .out(multiplexer_11_out), .sel(Stall_Signal));
  Register #(.width(1)) EX_MA_MemRW_Reg (.D(EX_MemRW), .clk(clk), .Q(MA_MemRW));  // open: en, clr
  Register #(.width(2)) EX_MA_WBSel_Reg (.D(EX_WBSel), .clk(clk), .Q(MA_WBSel));  // open: en, clr
  Register #(.width(1)) EX_MA_CSRSel_Reg (.D(EX_CSRSel), .clk(clk), .Q(MA_CSRSel));  // open: en, clr
  Register #(.width(1)) EX_MA_CSWen_Reg (.D(EX_CSRWen), .clk(clk), .Q(MA_CSRWen));  // open: en, clr
  Register #(.width(32)) MA_WB_Inst_Reg (.D(MA_Inst), .clk(clk), .Q(WB_Inst));  // open: en, clr
  Register #(.width(32)) EX_MA_RD2_Reg (.D(EX_RD2), .clk(clk), .Q(WRITE_DATA));  // open: en, clr
  Register #(.width(5)) MA_WB_RD_Reg (.D(MA_rd), .clk(clk), .Q(WB_rd));  // open: en, clr
  Register #(.width(1)) MA_WB_RegWEn_Reg (.D(MA_RegWEn), .clk(clk), .Q(WB_RegWEn));  // open: en, clr
  Register #(.width(32)) MA_WB_MUX_Reg (.D(Write_Data_t), .clk(clk), .Q(WB_WD));  // open: en, clr
  Register #(.width(1)) ID_EX_BSel_Reg (.D(multiplexer_12_out), .clk(clk), .Q(EX_BSel));  // open: en, clr
  Multiplexer #(.enable("false")) multiplexer_12 (.in0(BSel), .in1(1'b0), .out(multiplexer_12_out), .sel(Stall_Signal));
  Register #(.width(2)) MA_WB_WBSel_Reg (.D(MA_WBSel), .clk(clk), .Q(WB_WBSel));  // open: en, clr
  Register #(.width(1)) MA_WB_CSRSel_Reg (.D(MA_CSRSel), .clk(clk), .Q(WB_CSRSel));  // open: en, clr
  Register #(.width(1)) MA_WB_CSRWen_Reg (.D(MA_CSRWen), .clk(clk), .Q(WB_CSRWen));  // open: en, clr
  control_logic control_logic_1 (
    .CSRWen(CSRWen), .PCSel(PCSel), .RegWEn(RegWEn), .ImmSel(ImmSel), .BrUn(BrUn), .ASel(ASel), .BSel(BSel),
    .ALUSel(ALUSel), .MemRW(MemRW), .WBSel(WBSel), .CSRSel(CSRSel),
    .inst({funct7, ID_Inst[24:15], funct3, ID_Inst[11:0]}), .BrEq(BrEq), .BrLt(BrLt));
  regfile regfile_1 (
    .rs1(ID_Inst[19:15]), .rs2(ID_Inst[24:20]), .rd(WB_rd), .Write_Data(WB_WD), .RegWEn(WB_RegWEn),
    .clk(clk), .ra(ra), .sp(sp), .t0(t0), .t1(t1), .t2(t2), .s0(s0), .s1(s1), .a0(a0),
    .Read_Data_1(Read_Data_1), .Read_Data_2(Read_Data_2));
  branch_comp branch_comp_1 (.rs1(EX_RD1), .rs2(EX_RD2), .BrUn(EX_BrUn), .BrEq(BrEq), .BrLt(BrLt));
  imm_gen imm_gen_1 (.inst({EX_funct7, EX_Inst[24:15], EX_funct3, EX_Inst[11:0]}), .ImmSel(ImmSel), .imm(imm));
  csr csr_1 (.CSR_address(12'h51e), .CSR_din(CSR_Value), .CSR_WE(WB_CSRWen), .clk(clk), .tohost(tohost));
  BJK_Detector bjk_detector_1 (
    .EX_opcode(EX_Inst[6:0]), .EX_funct3(EX_funct3), .BrUN(EX_BrUn), .BrLt(EX_BrLt), .BrEq(EX_BrEq), .BJK(BJK));
  MRW_WE mrw_we_1 (.MemRW(MA_MemRW), .funct3(EX_funct3), .addr(EX_MA_RD2), .Write_Enable(WRITE_ENABLE));
  Forward_Detector forward_detector_1 (
    .EX_rs1(EX_Inst[19:15]), .EX_rs2(EX_Inst[24:20]), .MA_rd(MA_rd), .WB_rd(WB_rd), .MA_RegWEn(MA_RegWEn),
    .WB_RegWEn(WB_RegWEn), .EX_BSel(EX_BSel), .ForwardA(ForwardA), .ForwardB(ForwardB));
  Halt_Detector halt_detector_1 (.ID_Inst({funct7, ID_Inst[24:15], funct3, ID_Inst[11:0]}), .Halt_Signal(Halt_Signal));
  Stall_Detector stall_detector_1 (
    .rs1(ID_Inst[19:15]), .rs2(ID_Inst[24:20]), .EX_rd(EX_rd), .EX_MenRW(EX_RegWEn), .EX_RegWEn(EX_MemRW),
    .Stall_Signal(Stall_Signal));
  Multiplexer #(.enable("false"), .width(32)) multiplexer_13 (
    .in0(EX_RD2), .in1(imm), .out(multiplexer_13_out), .sel(EX_BSel));
  Multiplexer #(.enable("false"), .width(32)) multiplexer_14 (
    .in0(EX_RD1), .in1(EX_PC), .out(multiplexer_14_out));  // open: sel
  or or_2 (Freeze_Pipeline, Halt_Signal, Stall_Signal);
  Multiplexer #(.enable("false"), .width(32)) multiplexer_15 (
    .in0({funct7, ID_Inst[24:15], funct3, ID_Inst[11:0]}), .in1(32'h13), .out(ID_Inst_Input), .sel(BJK));
  Multiplexer #(.enable("false"), .width(32)) multiplexer_16 (
    .in0(EX_RD1), .in1(imm), .out(CSR_Value), .sel(WB_CSRSel));
  Multiplexer #(.enable("false"), .select(2), .width(32)) multiplexer_17 (
    .in0(WRITE_ADDRESS), .in1(READ_DATA), .in2(MA_PC), .out(Write_Data_t));  // open: in3, sel
  Multiplexer #(.enable("false"), .select(2), .width(32)) multiplexer_18 (
    .in0(multiplexer_14_out), .in1(WB_WD), .in2(WRITE_ADDRESS), .out(multiplexer_18_out));  // open: in3, sel
  Multiplexer #(.enable("false"), .select(2), .width(32)) multiplexer_19 (
    .in0(multiplexer_13_out), .in1(WRITE_ADDRESS), .in2(WB_WD), .out(multiplexer_19_out));  // open: in3, sel
  alu alu_1 (.Result(ALU_Res), .A(multiplexer_18_out), .B(multiplexer_19_out), .ALUSel(EX_ALUSel));

  // Other names for the same wires on the sheet: EX_opcode[6:0] = EX_Inst[6:0];
  //   EX_Inst (some bits) = {EX_funct7, EX_funct3}; EX_rs1[4:0] = EX_Inst[19:15]; EX_rs2[4:0] = EX_Inst[24:20];
  //   opcode[6:0] = ID_Inst[6:0]; rd[4:0] = ID_Inst[11:7]; ID_Inst (some bits) = {funct7, funct3};
  //   rs1[4:0] = ID_Inst[19:15]; rs2[4:0] = ID_Inst[24:20]; MA_ALU[31:0] = WRITE_ADDRESS; MA_RD2[31:0] = WRITE_DATA

  // Notes on the sheet:
  //   Output to IMEM
  //   IMEM (do **NOT** move this)
  //   Inputs from IMEM
  //   It is OK to move the PC, RegFile, ALU, MEM, Branch Comp, Imm Gen, and Control Logic to wherever is most convenient for you when constructing your CPU, and to delete this text
  //   Inputs/Outputs for testing. Do **NOT** move these.
  //   Outputs To DMEM
  //   DMEM (do **NOT** move this)
  //   Inputs From DMEM
endmodule

module BJK_Detector (
  input  [6:0] EX_opcode,
  input  [2:0] EX_funct3,
  input  BrUN,
  input  BrLt,
  input  BrEq,
  output BJK
);

  wire and_1_out, and_2_out, and_3_out, and_4_out, BEQ, BGE, BGEU, BLT, BLTU, BNE, BranchTaken,
       comparator_1_eq, comparator_2_eq, comparator_3_eq, comparator_4_eq, comparator_5_eq, comparator_6_eq,
       comparator_7_eq, comparator_8_eq, comparator_9_eq, JumpTaken, not_1_out, not_2_out, not_3_out,
       not_4_out, not_5_out, Opc_B, or_1_out, or_2_out, or_3_out, or_4_out, or_5_out, or_6_out;

  Comparator #(.width(3)) comparator_1 (.a(EX_funct3), .b(3'b000), .eq(comparator_1_eq));  // open: gt, lt
  Comparator #(.width(3)) comparator_2 (.a(EX_funct3), .b(3'b100), .eq(comparator_2_eq));  // open: gt, lt
  not not_1 (not_1_out, BrUN);
  and and_1 (and_1_out, not_1_out, BrLt);
  Comparator #(.width(3)) comparator_3 (.a(EX_funct3), .b(3'b101), .eq(comparator_3_eq));  // open: gt, lt
  not not_2 (not_2_out, BrUN);
  and and_2 (and_2_out, not_2_out, not_3_out);
  not not_3 (not_3_out, BrLt);
  Multiplexer #(.enable("false")) multiplexer_1 (.in0(1'b0), .in1(1'b1), .out(Opc_B), .sel(comparator_4_eq));
  Comparator #(.width(7)) comparator_4 (.a(EX_opcode), .b(7'b1100011), .eq(comparator_4_eq));  // open: gt, lt
  Multiplexer #(.enable("false")) multiplexer_2 (.in0(1'b0), .in1(comparator_1_eq), .out(BEQ), .sel(BrEq));
  Multiplexer #(.enable("false")) multiplexer_3 (.in0(1'b0), .in1(comparator_2_eq), .out(BLT), .sel(and_1_out));
  Multiplexer #(.enable("false")) multiplexer_4 (.in0(1'b0), .in1(comparator_3_eq), .out(BGE), .sel(and_2_out));
  Comparator #(.width(3)) comparator_5 (.a(EX_funct3), .b(3'b001), .eq(comparator_5_eq));  // open: gt, lt
  Comparator #(.width(3)) comparator_6 (.a(EX_funct3), .b(3'b110), .eq(comparator_6_eq));  // open: gt, lt
  Comparator #(.width(3)) comparator_7 (.a(EX_funct3), .b(3'b111), .eq(comparator_7_eq));  // open: gt, lt
  not not_4 (not_4_out, BrLt);
  Multiplexer #(.enable("false")) multiplexer_5 (.in0(1'b0), .in1(comparator_5_eq), .out(BNE), .sel(not_5_out));
  not not_5 (not_5_out, BrEq);
  Multiplexer #(.enable("false")) multiplexer_6 (.in0(1'b0), .in1(comparator_6_eq), .out(BLTU), .sel(and_3_out));
  and and_3 (and_3_out, BrUN, BrLt);
  Multiplexer #(.enable("false")) multiplexer_7 (.in0(1'b0), .in1(comparator_7_eq), .out(BGEU), .sel(and_4_out));
  and and_4 (and_4_out, BrUN, not_4_out);
  or or_1 (or_1_out, BEQ, BNE);
  or or_2 (or_2_out, BLT, BGE);
  or or_3 (or_3_out, BLTU, BGEU);
  or or_4 (or_4_out, or_1_out, or_2_out);
  or or_5 (or_5_out, or_2_out, or_3_out);
  Comparator #(.width(7)) comparator_8 (.a(7'b1100111), .b(EX_opcode), .eq(comparator_8_eq));  // open: gt, lt
  Comparator #(.width(7)) comparator_9 (.a(EX_opcode), .b(7'b1101111), .eq(comparator_9_eq));  // open: gt, lt
  or or_6 (or_6_out, or_4_out, or_5_out);
  or or_7 (JumpTaken, comparator_8_eq, comparator_9_eq);
  or or_8 (BJK, BranchTaken, JumpTaken);
  and and_5 (BranchTaken, or_6_out, Opc_B);

  // Notes on the sheet:
  //   Inputs
  //   Outputs
endmodule

module MRW_WE (
  input  MemRW,
  input  [2:0] funct3,
  input  [31:0] addr,
  output [3:0] Write_Enable
);

  wire [3:0] multiplexer_1_out, multiplexer_3_out, shifter_1_out;

  Shifter #(.width(4)) shifter_1 (.in(4'b0001), .\dist (addr[1:0]), .out(shifter_1_out));
  Multiplexer #(.enable("false"), .width(4)) multiplexer_1 (
    .in0(4'b0011), .in1(4'b1100), .out(multiplexer_1_out), .sel(addr[1]));
  Multiplexer #(.enable("false"), .width(4)) multiplexer_2 (
    .in0(4'b0000), .in1(multiplexer_3_out), .out(Write_Enable));  // open: sel
  Multiplexer #(.enable("false"), .select(3), .width(4)) multiplexer_3 (
    .in0(shifter_1_out), .in1(multiplexer_1_out), .in2(4'b1111), .in3(4'b0000), .in4(4'b0000), .in5(4'b0000),
    .in6(4'b0000), .in7(4'b0000), .out(multiplexer_3_out), .sel(funct3));

  // Other names for the same wires on the sheet: Address[31:0] = addr; low_ad[1:0] = addr[1:0];
  //   WE[3:0] = Write_Enable
endmodule

module Forward_Detector (
  input  [4:0] EX_rs1,
  input  [4:0] EX_rs2,
  input  [4:0] MA_rd,
  input  [4:0] WB_rd,
  input  MA_RegWEn,
  input  WB_RegWEn,
  input  EX_BSel,
  output [1:0] ForwardA,
  output [1:0] ForwardB
);

  wire comparator_1_eq, comparator_2_eq, comparator_3_eq, comparator_4_eq, comparator_5_eq, comparator_6_eq,
       comparator_7_eq, comparator_8_eq, EX_Hazard_B, not_1_out, not_2_out, not_3_out, not_4_out, not_5_out,
       not_6_out, WB_Hazard_A, WB_Hazard_B;
  wire [1:1] PreForwardB;

  not not_1 (not_1_out, comparator_1_eq);
  Comparator #(.width(5)) comparator_1 (.a(MA_rd), .b({5{1'b0}}), .eq(comparator_1_eq));  // open: gt, lt
  Comparator #(.width(5)) comparator_2 (.a(EX_rs1), .b(MA_rd), .eq(comparator_2_eq));  // open: gt, lt
  not not_2 (not_2_out, comparator_3_eq);
  Comparator #(.width(5)) comparator_3 (.a(WB_rd), .b({5{1'b0}}), .eq(comparator_3_eq));  // open: gt, lt
  Comparator #(.width(5)) comparator_4 (.a(WB_rd), .b(EX_rs1), .eq(comparator_4_eq));  // open: gt, lt
  not not_3 (not_3_out, ForwardA[1]);
  and and_1 (ForwardA[0], WB_Hazard_A, not_3_out);
  and and_2 (ForwardA[1], MA_RegWEn, not_1_out, comparator_2_eq);
  and and_3 (WB_Hazard_A, WB_RegWEn, not_2_out, comparator_4_eq);
  // Probe on ForwardB
  Multiplexer #(.enable("false"), .width(2)) multiplexer_1 (
    .in0({PreForwardB[1], EX_Hazard_B}), .in1(2'b00), .out(ForwardB), .sel(EX_BSel));
  Comparator #(.width(5)) comparator_5 (.a(MA_rd), .b({5{1'b0}}), .eq(comparator_5_eq));  // open: gt, lt
  Comparator #(.width(5)) comparator_6 (.a(EX_rs2), .b(MA_rd), .eq(comparator_6_eq));  // open: gt, lt
  Comparator #(.width(5)) comparator_7 (.a(WB_rd), .b({5{1'b0}}), .eq(comparator_7_eq));  // open: gt, lt
  Comparator #(.width(5)) comparator_8 (.a(WB_rd), .b(EX_rs2), .eq(comparator_8_eq));  // open: gt, lt
  not not_4 (not_4_out, EX_Hazard_B);
  not not_5 (not_5_out, comparator_5_eq);
  not not_6 (not_6_out, comparator_7_eq);
  and and_4 (PreForwardB[1], WB_Hazard_B, not_4_out);
  and and_5 (EX_Hazard_B, MA_RegWEn, not_5_out, comparator_6_eq);
  and and_6 (WB_Hazard_B, WB_RegWEn, not_6_out, comparator_8_eq);

  // Other names for the same wires on the sheet: EX_Hazard_A = ForwardA[1]; PreForwardB[0] = EX_Hazard_B
endmodule

module Halt_Detector (
  input  [31:0] ID_Inst,
  output Halt_Signal
);

  Comparator #(.width(32)) comparator_1 (.a(ID_Inst), .b({32{1'b0}}), .eq(Halt_Signal));  // open: gt, lt
endmodule

module Stall_Detector (
  input  [4:0] rs1,
  input  [4:0] rs2,
  input  [4:0] EX_rd,
  input  EX_MenRW,
  input  EX_RegWEn,
  output Stall_Signal
);

  wire and_1_out, and_2_out, comparator_1_eq, comparator_2_eq, comparator_3_eq, not_1_out, or_1_out;

  Comparator #(.width(5)) comparator_1 (.a(rs1), .b(EX_rd), .eq(comparator_1_eq));  // open: gt, lt
  Comparator #(.width(5)) comparator_2 (.a(rs2), .b(EX_rd), .eq(comparator_2_eq));  // open: gt, lt
  Comparator #(.width(5)) comparator_3 (.a(EX_rd), .b({5{1'b0}}), .eq(comparator_3_eq));  // open: gt, lt
  or or_1 (or_1_out, comparator_1_eq, comparator_2_eq);
  not not_1 (not_1_out, comparator_3_eq);
  and and_1 (and_1_out, EX_MenRW, EX_RegWEn);
  and and_2 (and_2_out, or_1_out, not_1_out);
  and and_3 (Stall_Signal, and_1_out, and_2_out);

  // Other names for the same wires on the sheet: rd[4:0] = EX_rd
endmodule
