// Logisim project csr.circ as structural Verilog: 1 circuit, main circuit csr
module csr (
  input  [11:0] CSR_address,
  input  [31:0] CSR_din,
  input  CSR_WE,
  input  clk,
  output [31:0] tohost
);

  wire Addr_Match, WE_final;

  Comparator #(.width(12)) comparator_1 (.a(CSR_address), .b(12'h51e), .eq(Addr_Match));  // open: gt, lt
  Register #(.width(32)) Reg_toHost (.D(CSR_din), .en(WE_final), .clk(clk), .Q(tohost));  // open: clr
  and and_1 (WE_final, Addr_Match, CSR_WE);

  // Other names for the same wires on the sheet: address[11:0] = CSR_address; data[31:0] = CSR_din; WE = CSR_WE

  // Notes on the sheet:
  //   INPUTS to your circuit
  //   DON'T CHANGE THE LOCATIONS OF THE INPUTS AND OUTPUTS!
  //   OUTPUT from your circuit
endmodule
