// Logisim project imm_gen.circ as structural Verilog: 1 circuit, main circuit imm_gen
module imm_gen (
  input  [31:0] inst,
  input  [2:0] ImmSel,
  output [31:0] imm
);

  wire [31:0] imm_B, imm_I, imm_J, imm_S;

  assign imm_I = {{20{inst[31]}}, inst[31:20]};  // Bit_Extender bit_extender_1
  assign imm_S = {{20{inst[31]}}, {inst[31:25], inst[11:7]}};  // Bit_Extender bit_extender_2
  assign imm_B = {{19{inst[31]}}, {inst[31], inst[7], inst[30:25], inst[11:8], 1'b0}};  // Bit_Extender bit_extender_3
  assign imm_J = {{11{inst[31]}}, {inst[31], inst[19:12], inst[20], inst[30:21], 1'b0}};  // Bit_Extender bit_extender_4
  Multiplexer #(.enable("false"), .select(3), .width(32)) multiplexer_1 (
    .in0({32{1'b0}}), .in1(imm_I), .in2(imm_S), .in3(imm_B), .in4({inst[31:12], {12{1'b0}}}), .in5(imm_J),
    .in6({32{1'b0}}), .out(imm), .sel(ImmSel));  // open: in7

  // Other names for the same wires on the sheet: imm_U[31:12] = inst[31:12]

  // Notes on the sheet:
  //   INPUTS to your circuit
  //   DON'T CHANGE THE LOCATIONS OF THE INPUTS AND OUTPUTS!
  //   OUTPUT from your circuit
endmodule
